// Logisim project Pipeline1.circ as structural Verilog
module upc (
  input  [5:0] opcode,
  output RegDst,
  output ALUSrc,
  output MemtoReg,
  output RegWrite,
  output MemRead,
  output MemWrite,
  output BranchEq,
  output ALUOp1,
  output AluOp0,
  output Jump,
  output BranchNEq
);

  wire and_2_out, and_3_out, and_4_out, not_1_out, not_2_out, not_3_out, not_4_out;

  not not_1 (not_1_out, opcode[3]);
  not not_2 (not_2_out, opcode[2]);
  not not_3 (not_3_out, opcode[1]);
  not not_4 (not_4_out, opcode[0]);
  and and_1 (RegDst, not_1_out, not_3_out);
  and and_2 (and_2_out, not_2_out, opcode[0]);
  and and_3 (and_3_out, not_2_out, not_3_out);
  and and_4 (and_4_out, not_1_out, not_2_out, opcode[0]);
  and and_5 (MemRead, not_1_out, not_2_out, opcode[0]);
  and and_6 (MemWrite, opcode[3], opcode[1]);
  and and_7 (BranchEq, opcode[2], not_4_out);
  and and_8 (ALUOp1, not_1_out, not_2_out, not_3_out);
  and and_9 (Jump, opcode[1], not_4_out);
  and and_10 (BranchNEq, not_3_out, opcode[0]);
  or or_1 (ALUSrc, opcode[3], and_2_out);
  or or_2 (RegWrite, and_3_out, and_4_out);

  assign AluOp0 = opcode[2];
  assign MemtoReg = opcode[0];
endmodule

module cpu (
  output [4:0] SHAMT,
  output [15:0] out_2,
  output [31:0] out_3,
  output [31:0] out_4,
  output [31:0] out_5,
  output [31:0] out_6,
  output [31:0] out_7,
  output [31:0] out_8,
  output [31:0] out_9,
  output [31:0] out_10,
  output [31:0] out_11,
  output [31:0] out_12,
  output [31:0] out_13
);

  wire alu_1_zero, and_1_out, and_2_out, bne, branch, clk, debug_1_add, debug_1_addi, debug_1_an,
       debug_1_beq, debug_1_bne, debug_1_jump, debug_1_load, debug_1_orr, debug_1_store, debug_1_sub,
       decodificador_1_c, decodificador_1_e, decodificador_1_f, decodificador_1_g, decodificador_1_out_5,
       decodificador_1_out_6, decodificador_1_out_8, decodificador_2_c, decodificador_2_e, decodificador_2_f,
       decodificador_2_g, decodificador_2_out_5, decodificador_2_out_6, decodificador_2_out_8,
       decodificador_3_c, decodificador_3_e, decodificador_3_f, decodificador_3_g, decodificador_3_out_5,
       decodificador_3_out_6, decodificador_3_out_8, decodificador_4_c, decodificador_4_e, decodificador_4_f,
       decodificador_4_g, decodificador_4_out_5, decodificador_4_out_6, decodificador_4_out_8,
       decodificador_5_c, decodificador_5_e, decodificador_5_f, decodificador_5_g, decodificador_5_out_5,
       decodificador_5_out_6, decodificador_5_out_8, decodificador_6_c, decodificador_6_e, decodificador_6_f,
       decodificador_6_g, decodificador_6_out_5, decodificador_6_out_6, decodificador_6_out_8,
       decodificador_7_c, decodificador_7_e, decodificador_7_f, decodificador_7_g, decodificador_7_out_5,
       decodificador_7_out_6, decodificador_7_out_8, decodificador_8_c, decodificador_8_e, decodificador_8_f,
       decodificador_8_g, decodificador_8_out_5, decodificador_8_out_6, decodificador_8_out_8,
       decodificador_9_c, decodificador_9_e, decodificador_9_f, decodificador_9_g, decodificador_9_out_5,
       decodificador_9_out_6, decodificador_9_out_8, decodificador_10_c, decodificador_10_e,
       decodificador_10_f, decodificador_10_g, decodificador_10_out_5, decodificador_10_out_6,
       decodificador_10_out_8, ex_mem_1_jumppout, ex_mem_1_memtoregout, ex_mem_1_memwrout, ex_mem_1_regwrout,
       id_ex_1_alusrcout, id_ex_1_brancheqout, id_ex_1_branchneqout, id_ex_1_jumppout, id_ex_1_memtoregout,
       id_ex_1_memwrout, id_ex_1_regdestout, id_ex_1_regwrout, jumpp, mem_wr_1_memtoregout, not_1_out,
       or_1_out, RegDst, regwrmemwr, res, upc_1_alusrc, upc_1_brancheq, upc_1_branchneq, upc_1_jump,
       upc_1_memtoreg, upc_1_memwrite, upc_1_regwrite, zero;
  wire [1:0] upc_1_aluop0;
  wire [3:0] alucontrol_1_aluopout, ex_mem_1_pctestout, ex_mem_1_pctestout_2, ex_mem_1_pctestout_4,
       id_ex_1_aluopout, id_ex_1_pcout, id_ex_1_pcout_2, id_ex_1_pcout_4, if_id_1_pcout, if_id_1_pcout_2,
       if_id_1_pcout_4;
  wire [4:0] ex_mem_1_rwout, id_ex_1_rdout, id_ex_1_rtout, multiplexer_3_out, RD, RS, RT, rwmemwr;
  wire [5:0] func, opc;
  wire [11:0] ex_mem_1_pctestout_3, id_ex_1_pcout_3, if_id_1_pcout_3;
  wire [15:0] id_ex_1_immout;
  wire [23:0] adder_2_out, bit_extender_1_out, bit_extender_3_out, bit_extender_4_out, mem_wr_1_pctestout,
       multiplexer_1_out, multiplexer_2_out, multiplexer_5_out, PC, pcexmem, register_1_q, subtractor_1_out;
  wire [25:0] jump;
  wire [31:0] alu_1_dataout, bit_extender_2_out, busmemwr, ex_mem_1_busbout, ex_mem_1_dataout, id_ex_1_raout,
       id_ex_1_rbout, if_id_1_instout, mem_wr_1_dataout, mem_wr_1_dataprevout, multiplexer_4_out, ram_1_dout,
       ram_2_dout, ur_1_rra;

  not not_1 (not_1_out, zero);
  and and_1 (and_1_out, zero, branch);
  and and_2 (and_2_out, not_1_out, bne);
  or or_1 (or_1_out, and_1_out, and_2_out);
  upc upc_1 (
    .opcode(opc), .RegDst(RegDst), .ALUSrc(upc_1_alusrc), .MemtoReg(upc_1_memtoreg),
    .RegWrite(upc_1_regwrite), .MemWrite(upc_1_memwrite), .BranchEq(upc_1_brancheq),
    .ALUOp1(upc_1_aluop0[1]), .AluOp0(upc_1_aluop0[0]), .Jump(upc_1_jump), .BranchNEq(upc_1_branchneq));  // open: MemRead
  Multiplexer #(.width(24)) multiplexer_1 (.in0(PC), .in1(pcexmem), .out(multiplexer_1_out), .sel(or_1_out));
  Bit_Extender #(.in_width(26), .out_width(24)) bit_extender_1 (.in(jump), .out(bit_extender_1_out));
  UR ur_1 (
    .clk(clk), .data(busmemwr), .rst(res), .regw(regwrmemwr), .rw(rwmemwr), .ra(RS), .rb(RT), .r8_t0(out_8),
    .r9_t1(out_4), .r10_t2(out_5), .r11_t3(out_6), .r12_t4(out_7), .r13_t5(out_13), .r14_t6(out_9),
    .r15_t7(out_10), .Rra(ur_1_rra), .Rrb(out_3), .r24_t7(out_11), .r25_t8(out_12));
  Register #(.width(24)) register_1 (.D(multiplexer_2_out), .clk(clk), .Q(register_1_q), .clr(res));  // open: en
  Multiplexer #(.width(24)) multiplexer_2 (
    .in0(multiplexer_1_out), .in1(bit_extender_1_out), .out(multiplexer_2_out), .sel(1'b0));
  Adder #(.width(24)) adder_1 (.a(24'h1), .b(register_1_q), .out(PC));  // open: cin, cout
  RAM #(.addrWidth(24), .dataWidth(32), .enables("line")) ram_1 (
    .addr(register_1_q), .clk(clk), .dout(ram_1_dout));  // open: we, din
  alucontrol alucontrol_1 (.aluop(upc_1_aluop0), .funct(func), .aluopout(alucontrol_1_aluopout));
  Button button_1 (.out(res));
  Clock clock_1 (.out(clk));
  decodificador decodificador_1 (
    .D(PC[7]), .in_2(PC[6]), .B(PC[5]), .A(PC[4]), .out_5(decodificador_1_out_5),
    .out_6(decodificador_1_out_6), .c(decodificador_1_c), .out_8(decodificador_1_out_8),
    .e(decodificador_1_e), .f(decodificador_1_f), .g(decodificador_1_g));
  ID_EX id_ex_1 (
    .alusrc(upc_1_alusrc), .aluop(alucontrol_1_aluopout), .imm(out_2), .memwr(upc_1_memwrite),
    .pc({if_id_1_pcout_4, if_id_1_pcout_3, if_id_1_pcout_2, if_id_1_pcout}), .regwr(upc_1_regwrite),
    .memtoreg(upc_1_memtoreg), .branchneq(upc_1_branchneq), .clk(clk), .brancheq(upc_1_brancheq), .rst(res),
    .jumpp(upc_1_jump), .ra(ur_1_rra), .rb(out_3), .rt(RT), .rd(RD), .regdest(RegDst),
    .alusrcout(id_ex_1_alusrcout), .aluopout(id_ex_1_aluopout), .immout(id_ex_1_immout),
    .memwrout(id_ex_1_memwrout), .pcout({id_ex_1_pcout_4, id_ex_1_pcout_3, id_ex_1_pcout_2, id_ex_1_pcout}),
    .regwrout(id_ex_1_regwrout), .memtoregout(id_ex_1_memtoregout), .branchneqout(id_ex_1_branchneqout),
    .brancheqout(id_ex_1_brancheqout), .jumppout(id_ex_1_jumppout), .raout(id_ex_1_raout),
    .rbout(id_ex_1_rbout), .rtout(id_ex_1_rtout), .rdout(id_ex_1_rdout), .regdestout(id_ex_1_regdestout));
  IF_ID if_id_1 (
    .inst(ram_1_dout), .pc(PC), .clk(clk), .reset(res), .instout(if_id_1_instout),
    .pcout({if_id_1_pcout_4, if_id_1_pcout_3, if_id_1_pcout_2, if_id_1_pcout}));
  _7_Segment_Display u_7_segment_display_1 (
    .g(decodificador_1_g), .f(decodificador_1_f), .a(decodificador_1_out_5), .b(decodificador_1_out_6),
    .e(decodificador_1_e), .d(decodificador_1_out_8), .c(decodificador_1_c));  // open: dp
  assign bit_extender_2_out = {{16{id_ex_1_immout[15]}}, id_ex_1_immout};  // Bit_Extender bit_extender_2
  Multiplexer #(.width(5)) multiplexer_3 (
    .in0(id_ex_1_rtout), .in1(id_ex_1_rdout), .out(multiplexer_3_out), .sel(id_ex_1_regdestout));
  Multiplexer #(.width(32)) multiplexer_4 (
    .in0(id_ex_1_rbout), .in1(bit_extender_2_out), .out(multiplexer_4_out), .sel(id_ex_1_alusrcout));
  decodificador decodificador_2 (
    .D(PC[3]), .in_2(PC[2]), .B(PC[1]), .A(PC[0]), .out_5(decodificador_2_out_5),
    .out_6(decodificador_2_out_6), .c(decodificador_2_c), .out_8(decodificador_2_out_8),
    .e(decodificador_2_e), .f(decodificador_2_f), .g(decodificador_2_g));
  Spliter spliter_1 (
    .ENTRADA(if_id_1_instout), .jump(jump), .funct(func), .sham(SHAMT), .off(out_2), .rd(RD), .rs(RS),
    .opcode(opc), .rt(RT));
  _7_Segment_Display u_7_segment_display_2 (
    .g(decodificador_2_g), .f(decodificador_2_f), .a(decodificador_2_out_5), .b(decodificador_2_out_6),
    .e(decodificador_2_e), .d(decodificador_2_out_8), .c(decodificador_2_c));  // open: dp
  assign bit_extender_3_out = {{9{id_ex_1_immout[14]}}, id_ex_1_immout[14:0]};  // Bit_Extender bit_extender_3
  alu alu_1 (
    .d1(id_ex_1_raout), .d2(multiplexer_4_out), .Aluop(id_ex_1_aluopout), .dataout(alu_1_dataout),
    .zero(alu_1_zero));
  Adder #(.width(24)) adder_2 (
    .a({id_ex_1_pcout_4, id_ex_1_pcout_3, id_ex_1_pcout_2, id_ex_1_pcout}), .b(bit_extender_3_out),
    .out(adder_2_out));  // open: cin, cout
  Subtractor #(.width(24)) subtractor_1 (
    .a({id_ex_1_pcout_4, id_ex_1_pcout_3, id_ex_1_pcout_2, id_ex_1_pcout}), .b(bit_extender_3_out),
    .out(subtractor_1_out));  // open: bin, bout
  Multiplexer #(.width(24)) multiplexer_5 (
    .in0(adder_2_out), .in1(subtractor_1_out), .out(multiplexer_5_out), .sel(id_ex_1_immout[15]));
  decodificador decodificador_3 (
    .D(if_id_1_pcout_2[3]), .in_2(if_id_1_pcout_2[2]), .B(if_id_1_pcout_2[1]), .A(if_id_1_pcout_2[0]),
    .out_5(decodificador_3_out_5), .out_6(decodificador_3_out_6), .c(decodificador_3_c),
    .out_8(decodificador_3_out_8), .e(decodificador_3_e), .f(decodificador_3_f), .g(decodificador_3_g));
  decodificador decodificador_4 (
    .D(id_ex_1_pcout_2[3]), .in_2(id_ex_1_pcout_2[2]), .B(id_ex_1_pcout_2[1]), .A(id_ex_1_pcout_2[0]),
    .out_5(decodificador_4_out_5), .out_6(decodificador_4_out_6), .c(decodificador_4_c),
    .out_8(decodificador_4_out_8), .e(decodificador_4_e), .f(decodificador_4_f), .g(decodificador_4_g));
  _7_Segment_Display u_7_segment_display_3 (
    .g(decodificador_3_g), .f(decodificador_3_f), .a(decodificador_3_out_5), .b(decodificador_3_out_6),
    .e(decodificador_3_e), .d(decodificador_3_out_8), .c(decodificador_3_c));  // open: dp
  EX_MEM ex_mem_1 (
    .pc(multiplexer_5_out), .rb(id_ex_1_rbout), .memwr(id_ex_1_memwrout), .data(alu_1_dataout),
    .branchEq(id_ex_1_brancheqout), .zero(alu_1_zero), .branchNeq(id_ex_1_branchneqout),
    .memtoreg(id_ex_1_memtoregout), .jumpp(id_ex_1_jumppout), .regwr(id_ex_1_regwrout), .clk(clk), .rst(res),
    .rw(multiplexer_3_out), .pctest({id_ex_1_pcout_4, id_ex_1_pcout_3, id_ex_1_pcout_2, id_ex_1_pcout}),
    .pcout(pcexmem), .busbout(ex_mem_1_busbout), .memwrout(ex_mem_1_memwrout), .dataout(ex_mem_1_dataout),
    .branchEqout(branch), .zeroout(zero), .branchNeqout(bne), .memtoregout(ex_mem_1_memtoregout),
    .jumppout(ex_mem_1_jumppout), .regwrout(ex_mem_1_regwrout), .rwout(ex_mem_1_rwout),
    .pctestout({ex_mem_1_pctestout_4, ex_mem_1_pctestout_3, ex_mem_1_pctestout_2, ex_mem_1_pctestout}));
  _7_Segment_Display u_7_segment_display_4 (
    .g(decodificador_4_g), .f(decodificador_4_f), .a(decodificador_4_out_5), .b(decodificador_4_out_6),
    .e(decodificador_4_e), .d(decodificador_4_out_8), .c(decodificador_4_c));  // open: dp
  decodificador decodificador_5 (
    .D(if_id_1_pcout[3]), .in_2(if_id_1_pcout[2]), .B(if_id_1_pcout[1]), .A(if_id_1_pcout[0]),
    .out_5(decodificador_5_out_5), .out_6(decodificador_5_out_6), .c(decodificador_5_c),
    .out_8(decodificador_5_out_8), .e(decodificador_5_e), .f(decodificador_5_f), .g(decodificador_5_g));
  decodificador decodificador_6 (
    .D(id_ex_1_pcout[3]), .in_2(id_ex_1_pcout[2]), .B(id_ex_1_pcout[1]), .A(id_ex_1_pcout[0]),
    .out_5(decodificador_6_out_5), .out_6(decodificador_6_out_6), .c(decodificador_6_c),
    .out_8(decodificador_6_out_8), .e(decodificador_6_e), .f(decodificador_6_f), .g(decodificador_6_g));
  _7_Segment_Display u_7_segment_display_5 (
    .g(decodificador_5_g), .f(decodificador_5_f), .a(decodificador_5_out_5), .b(decodificador_5_out_6),
    .e(decodificador_5_e), .d(decodificador_5_out_8), .c(decodificador_5_c));  // open: dp
  _7_Segment_Display u_7_segment_display_6 (
    .g(decodificador_6_g), .f(decodificador_6_f), .a(decodificador_6_out_5), .b(decodificador_6_out_6),
    .e(decodificador_6_e), .d(decodificador_6_out_8), .c(decodificador_6_c));  // open: dp
  Bit_Extender #(.in_width(32), .out_width(24)) bit_extender_4 (.in(ex_mem_1_dataout), .out(bit_extender_4_out));
  RAM #(.addrWidth(24), .dataWidth(32), .enables("line")) ram_2 (
    .addr(bit_extender_4_out), .we(ex_mem_1_memwrout), .clk(clk), .din(ex_mem_1_busbout), .dout(ram_2_dout));
  decodificador decodificador_7 (
    .D(ex_mem_1_pctestout_2[3]), .in_2(ex_mem_1_pctestout_2[2]), .B(ex_mem_1_pctestout_2[1]),
    .A(ex_mem_1_pctestout_2[0]), .out_5(decodificador_7_out_5), .out_6(decodificador_7_out_6),
    .c(decodificador_7_c), .out_8(decodificador_7_out_8), .e(decodificador_7_e), .f(decodificador_7_f),
    .g(decodificador_7_g));
  _7_Segment_Display u_7_segment_display_7 (
    .g(decodificador_7_g), .f(decodificador_7_f), .a(decodificador_7_out_5), .b(decodificador_7_out_6),
    .e(decodificador_7_e), .d(decodificador_7_out_8), .c(decodificador_7_c));  // open: dp
  debug debug_1 (
    .opcode(opc), .functioncode(func), .ADD(debug_1_add), .SUB(debug_1_sub), .AN(debug_1_an),
    .ORR(debug_1_orr), .ADDI(debug_1_addi), .LOAD(debug_1_load), .STORE(debug_1_store), .BEQ(debug_1_beq),
    .BNE(debug_1_bne), .JUMP(debug_1_jump));
  LED led_1 (.in(debug_1_add));
  LED led_2 (.in(debug_1_sub));
  LED led_3 (.in(debug_1_an));
  LED led_4 (.in(debug_1_orr));
  LED led_5 (.in(debug_1_addi));
  LED led_6 (.in(debug_1_load));
  LED led_7 (.in(debug_1_store));
  LED led_8 (.in(debug_1_beq));
  LED led_9 (.in(debug_1_bne));
  LED led_10 (.in(debug_1_jump));
  decodificador decodificador_8 (
    .D(ex_mem_1_pctestout[3]), .in_2(ex_mem_1_pctestout[2]), .B(ex_mem_1_pctestout[1]),
    .A(ex_mem_1_pctestout[0]), .out_5(decodificador_8_out_5), .out_6(decodificador_8_out_6),
    .c(decodificador_8_c), .out_8(decodificador_8_out_8), .e(decodificador_8_e), .f(decodificador_8_f),
    .g(decodificador_8_g));
  _7_Segment_Display u_7_segment_display_8 (
    .g(decodificador_8_g), .f(decodificador_8_f), .a(decodificador_8_out_5), .b(decodificador_8_out_6),
    .e(decodificador_8_e), .d(decodificador_8_out_8), .c(decodificador_8_c));  // open: dp
  MEM_WR mem_wr_1 (
    .rw(ex_mem_1_rwout), .jumpp(ex_mem_1_jumppout), .memtoreg(ex_mem_1_memtoregout), .data(ram_2_dout),
    .dataprev(ex_mem_1_dataout), .regwr(ex_mem_1_regwrout), .clk(clk), .rst(res),
    .pctest({ex_mem_1_pctestout_4, ex_mem_1_pctestout_3, ex_mem_1_pctestout_2, ex_mem_1_pctestout}),
    .rwout(rwmemwr), .jumppout(jumpp), .memtoregout(mem_wr_1_memtoregout), .dataout(mem_wr_1_dataout),
    .dataprevout(mem_wr_1_dataprevout), .regwrout(regwrmemwr), .pctestout(mem_wr_1_pctestout));
  Multiplexer #(.width(32)) multiplexer_6 (
    .in0(mem_wr_1_dataprevout), .in1(mem_wr_1_dataout), .out(busmemwr), .sel(mem_wr_1_memtoregout));
  decodificador decodificador_9 (
    .D(mem_wr_1_pctestout[7]), .in_2(mem_wr_1_pctestout[6]), .B(mem_wr_1_pctestout[5]),
    .A(mem_wr_1_pctestout[4]), .out_5(decodificador_9_out_5), .out_6(decodificador_9_out_6),
    .c(decodificador_9_c), .out_8(decodificador_9_out_8), .e(decodificador_9_e), .f(decodificador_9_f),
    .g(decodificador_9_g));
  _7_Segment_Display u_7_segment_display_9 (
    .g(decodificador_9_g), .f(decodificador_9_f), .a(decodificador_9_out_5), .b(decodificador_9_out_6),
    .e(decodificador_9_e), .d(decodificador_9_out_8), .c(decodificador_9_c));  // open: dp
  decodificador decodificador_10 (
    .D(mem_wr_1_pctestout[3]), .in_2(mem_wr_1_pctestout[2]), .B(mem_wr_1_pctestout[1]),
    .A(mem_wr_1_pctestout[0]), .out_5(decodificador_10_out_5), .out_6(decodificador_10_out_6),
    .c(decodificador_10_c), .out_8(decodificador_10_out_8), .e(decodificador_10_e), .f(decodificador_10_f),
    .g(decodificador_10_g));
  _7_Segment_Display u_7_segment_display_10 (
    .g(decodificador_10_g), .f(decodificador_10_f), .a(decodificador_10_out_5), .b(decodificador_10_out_6),
    .e(decodificador_10_e), .d(decodificador_10_out_8), .c(decodificador_10_c));  // open: dp

  // Other names for the same wires on the sheet: imm[15:0] = out_2; pcori[23:0] = PC; t0[31:0] = out_8;
  //   t1[31:0] = out_4; t2[31:0] = out_5; t3[31:0] = out_6; t4[31:0] = out_7; t5[31:0] = out_13; t6[31:0] = out_9;
  //   t7[31:0] = out_10; t8[31:0] = out_11; t9[31:0] = out_12
endmodule

module Spliter (
  input  [31:0] ENTRADA,
  output [4:0] rt,
  output [5:0] funct,
  output [4:0] sham,
  output [5:0] opcode,
  output [4:0] rd,
  output [4:0] rs,
  output [15:0] off,
  output [25:0] jump
);


  assign funct = ENTRADA[5:0];
  assign jump = ENTRADA[25:0];
  assign off = ENTRADA[15:0];
  assign opcode = ENTRADA[31:26];
  assign rd = ENTRADA[15:11];
  assign rs = ENTRADA[25:21];
  assign rt = ENTRADA[20:16];
  assign sham = ENTRADA[10:6];
endmodule

module alucontrol (
  input  [1:0] aluop,
  input  [5:0] funct,
  output [3:0] aluopout
);

  wire not_1_out, not_2_out, or_1_out, or_2_out, or_4_out;

  not not_1 (not_1_out, aluop[1]);
  not not_2 (not_2_out, funct[2]);
  or or_1 (or_1_out, aluop[1], aluop[0]);
  or or_2 (or_2_out, aluop[0], funct[1]);
  or or_3 (aluopout[1], not_1_out, not_2_out);
  or or_4 (or_4_out, funct[3], funct[0]);
  and and_1 (aluopout[2], or_1_out, or_2_out);
  and and_2 (aluopout[0], aluop[1], or_4_out);

  assign aluopout[3] = 1'b1;
endmodule

module debug (
  input  [5:0] opcode,
  input  [5:0] functioncode,
  output ADD,
  output SUB,
  output AN,
  output ORR,
  output ADDI,
  output LOAD,
  output STORE,
  output BEQ,
  output BNE,
  output JUMP
);

  wire not_1_out, not_2_out, not_3_out, not_4_out, not_5_out, not_6_out, not_7_out, not_8_out;

  not not_1 (not_1_out, opcode[5]);
  not not_2 (not_2_out, opcode[3]);
  not not_3 (not_3_out, opcode[2]);
  not not_4 (not_4_out, opcode[1]);
  not not_5 (not_5_out, opcode[0]);
  not not_6 (not_6_out, functioncode[2]);
  not not_7 (not_7_out, functioncode[1]);
  not not_8 (not_8_out, functioncode[0]);
  and and_1 (ADD, not_2_out, not_3_out, not_4_out, not_6_out, not_7_out);
  and and_2 (SUB, not_2_out, not_3_out, not_4_out, functioncode[1]);
  and and_3 (AN, not_2_out, not_3_out, not_4_out, functioncode[2], not_8_out);
  and and_4 (ORR, not_2_out, not_3_out, not_4_out, functioncode[0]);
  and and_5 (ADDI, opcode[3], not_4_out);
  and and_6 (LOAD, not_2_out, not_3_out, opcode[0]);
  and and_7 (STORE, opcode[3], opcode[0]);
  and and_8 (BEQ, opcode[2], not_5_out);
  and and_9 (BNE, not_4_out, opcode[0]);
  and and_10 (JUMP, not_1_out, opcode[1]);
endmodule

module UR (
  input  clk,
  input  [31:0] data,
  input  rst,
  input  regw,
  input  [4:0] rw,
  input  [4:0] ra,
  input  [4:0] rb,
  output [31:0] r8_t0,
  output [31:0] r9_t1,
  output [31:0] r10_t2,
  output [31:0] r11_t3,
  output [31:0] r12_t4,
  output [31:0] r13_t5,
  output [31:0] r14_t6,
  output [31:0] r15_t7,
  output [31:0] Rra,
  output [31:0] Rrb,
  output [31:0] r24_t7,
  output [31:0] r25_t8
);

  wire R0W, R1W, R2W, R3W, R4W, R5W, R6W, R7W, R8W, R9W, R10W, R11W, R12W, R13W, R14W, R15W, R16W, R17W,
       R18W, R19W, R20W, R21W, R22W, R23W, R24W, R25W, R26W, R27W, R28W, R29W, R30W, R31W;
  wire [31:0] R0, R1, R2, R3, R4, R5, R6, R7, R16, R17, R18, R19, R20, R21, R22, R23, R26, R27, R28, R29,
       R30, R31;

  Register #(.width(32)) register_1 (.D(data), .en(R0W), .Q(R0), .clk(clk), .clr(rst));
  Register #(.width(32)) register_2 (.D(data), .en(R8W), .Q(r8_t0), .clk(clk), .clr(rst));
  Register #(.width(32)) register_3 (.D(data), .en(R16W), .Q(R16), .clk(clk), .clr(rst));
  Register #(.width(32)) register_4 (.D(data), .en(R24W), .Q(r24_t7), .clk(clk), .clr(rst));
  Register #(.width(32)) register_5 (.D(data), .en(R1W), .Q(R1), .clk(clk), .clr(rst));
  Register #(.width(32)) register_6 (.D(data), .en(R9W), .Q(r9_t1), .clk(clk), .clr(rst));
  Register #(.width(32)) register_7 (.D(data), .en(R17W), .Q(R17), .clk(clk), .clr(rst));
  Register #(.width(32)) register_8 (.D(data), .en(R25W), .Q(r25_t8), .clk(clk), .clr(rst));
  Multiplexer #(.select(5), .width(32)) multiplexer_1 (
    .in0(R0), .in1(R1), .in2(R2), .in3(R3), .in4(R4), .in5(R5), .in6(R6), .in7(R7), .in8(r8_t0), .in9(r9_t1),
    .in10(r10_t2), .in11(r11_t3), .in12(r12_t4), .in13(r13_t5), .in14(r14_t6), .in15(r15_t7), .in16(R16),
    .in17(R17), .in18(R18), .in19(R19), .in20(R20), .in21(R21), .in22(R22), .in23(R23), .in24(r24_t7),
    .in25(r25_t8), .in26(R26), .in27(R27), .in28(R28), .in29(R29), .in30(R30), .in31(R31), .out(Rra), .sel(ra));
  Register #(.width(32)) register_9 (.D(data), .en(R10W), .Q(r10_t2), .clk(clk), .clr(rst));
  Register #(.width(32)) register_10 (.D(data), .en(R18W), .Q(R18), .clk(clk), .clr(rst));
  Register #(.width(32)) register_11 (.D(data), .en(R26W), .Q(R26), .clk(clk), .clr(rst));
  Register #(.width(32)) register_12 (.D(data), .en(R2W), .Q(R2), .clk(clk), .clr(rst));
  Register #(.width(32)) register_13 (.D(data), .en(R11W), .Q(r11_t3), .clk(clk), .clr(rst));
  Register #(.width(32)) register_14 (.D(data), .en(R19W), .Q(R19), .clk(clk), .clr(rst));
  Register #(.width(32)) register_15 (.D(data), .en(R3W), .Q(R3), .clk(clk), .clr(rst));
  Register #(.width(32)) register_16 (.D(data), .en(R27W), .Q(R27), .clk(clk), .clr(rst));
  Multiplexer #(.select(5), .width(32)) multiplexer_2 (
    .in0(R0), .in1(R1), .in2(R2), .in3(R3), .in4(R4), .in5(R5), .in6(R6), .in7(R7), .in8(r8_t0), .in9(r9_t1),
    .in10(r10_t2), .in11(r11_t3), .in12(r12_t4), .in13(r13_t5), .in14(r14_t6), .in15(r15_t7), .in16(R16),
    .in17(R17), .in18(R18), .in19(R19), .in20(R20), .in21(R21), .in22(R22), .in23(R23), .in24(r24_t7),
    .in25(r25_t8), .in26(R26), .in27(R27), .in28(R28), .in29(R29), .in30(R30), .in31(R31), .out(Rrb), .sel(rb));
  Register #(.width(32)) register_17 (.D(data), .en(R4W), .Q(R4), .clk(clk), .clr(rst));
  Register #(.width(32)) register_18 (.D(data), .en(R12W), .Q(r12_t4), .clk(clk), .clr(rst));
  Register #(.width(32)) register_19 (.D(data), .en(R20W), .Q(R20), .clk(clk), .clr(rst));
  Register #(.width(32)) register_20 (.D(data), .en(R28W), .Q(R28), .clk(clk), .clr(rst));
  Register #(.width(32)) register_21 (.D(data), .en(R5W), .Q(R5), .clk(clk), .clr(rst));
  Register #(.width(32)) register_22 (.D(data), .en(R13W), .Q(r13_t5), .clk(clk), .clr(rst));
  Register #(.width(32)) register_23 (.D(data), .en(R21W), .Q(R21), .clk(clk), .clr(rst));
  Register #(.width(32)) register_24 (.D(data), .en(R29W), .Q(R29), .clk(clk), .clr(rst));
  Register #(.width(32)) register_25 (.D(data), .en(R6W), .Q(R6), .clk(clk), .clr(rst));
  Register #(.width(32)) register_26 (.D(data), .en(R14W), .Q(r14_t6), .clk(clk), .clr(rst));
  Register #(.width(32)) register_27 (.D(data), .en(R22W), .Q(R22), .clk(clk), .clr(rst));
  Register #(.width(32)) register_28 (.D(data), .en(R30W), .Q(R30), .clk(clk), .clr(rst));
  Demultiplexer #(.select(5)) demultiplexer_1 (
    .out0(R0W), .out1(R1W), .out2(R2W), .out3(R3W), .out4(R4W), .out5(R5W), .out6(R6W), .out7(R7W),
    .out8(R8W), .out9(R9W), .out10(R10W), .out11(R11W), .out12(R12W), .out13(R13W), .out14(R14W),
    .out15(R15W), .out16(R16W), .out17(R17W), .out18(R18W), .out19(R19W), .out20(R20W), .out21(R21W),
    .out22(R22W), .out23(R23W), .out24(R24W), .out25(R25W), .out26(R26W), .out27(R27W), .out28(R28W),
    .out29(R29W), .out30(R30W), .out31(R31W), .in(regw), .sel(rw));
  Register #(.width(32)) register_29 (.D(data), .en(R15W), .Q(r15_t7), .clk(clk), .clr(rst));
  Register #(.width(32)) register_30 (.D(data), .en(R23W), .Q(R23), .clk(clk), .clr(rst));
  Register #(.width(32)) register_31 (.D(data), .en(R31W), .Q(R31), .clk(clk), .clr(rst));
  Register #(.width(32)) register_32 (.D(data), .en(R7W), .Q(R7), .clk(clk), .clr(rst));

  // Other names for the same wires on the sheet: R8[31:0] = r8_t0; R9[31:0] = r9_t1; R10[31:0] = r10_t2;
  //   R11[31:0] = r11_t3; R12[31:0] = r12_t4; R13[31:0] = r13_t5; R14[31:0] = r14_t6; R15[31:0] = r15_t7;
  //   R24[31:0] = r24_t7; R25[31:0] = r25_t8
endmodule

module alu (
  input  [31:0] d1,
  input  [31:0] d2,
  input  [3:0] Aluop,
  output [31:0] dataout,
  output zero
);

  wire [31:0] addd, andd, orr, subb;

  assign andd = d1 & d2;  // AND_Gate and_1, 32 bits wide
  assign orr = d1 | d2;  // OR_Gate or_1, 32 bits wide
  Adder #(.width(32)) adder_1 (.a(d1), .b(d2), .out(addd));  // open: cin, cout
  Subtractor #(.width(32)) subtractor_1 (.a(d1), .b(d2), .out(subb));  // open: bin, bout
  Multiplexer #(.select(4), .width(32)) multiplexer_1 (
    .in8(andd), .in9(orr), .in10(addd), .in14(subb), .out(dataout), .sel(Aluop));  // open: in0, in1, in2, in3, in4, in5, in6, in7, in11, in12, in13, in15
  Comparator #(.width(32)) comparator_1 (.a(dataout), .b({32{1'b0}}), .eq(zero));  // open: gt, lt
endmodule

module IF_ID (
  input  [31:0] inst,
  input  [23:0] pc,
  input  clk,
  input  reset,
  output [31:0] instout,
  output [23:0] pcout
);

  Register #(.width(32)) register_1 (.D(inst), .en(1'b1), .clk(clk), .Q(instout), .clr(reset));
  Register #(.width(24)) register_2 (.D(pc), .en(1'b1), .clk(clk), .Q(pcout), .clr(reset));
endmodule

module ID_EX (
  input  alusrc,
  input  [3:0] aluop,
  input  [15:0] imm,
  input  memwr,
  input  [23:0] pc,
  input  regwr,
  input  memtoreg,
  input  branchneq,
  input  clk,
  input  brancheq,
  input  rst,
  input  jumpp,
  input  [31:0] ra,
  input  [31:0] rb,
  input  [4:0] rt,
  input  [4:0] rd,
  input  regdest,
  output alusrcout,
  output [3:0] aluopout,
  output [15:0] immout,
  output memwrout,
  output [23:0] pcout,
  output regwrout,
  output memtoregout,
  output branchneqout,
  output brancheqout,
  output jumppout,
  output [31:0] raout,
  output [31:0] rbout,
  output [4:0] rtout,
  output [4:0] rdout,
  output regdestout
);

  Register #(.width(1)) register_1 (.D(alusrc), .en(1'b1), .clk(clk), .Q(alusrcout), .clr(rst));
  Register #(.width(4)) register_2 (.D(aluop), .en(1'b1), .clk(clk), .Q(aluopout), .clr(rst));
  Register #(.width(16)) register_3 (.D(imm), .en(1'b1), .clk(clk), .Q(immout), .clr(rst));
  Register #(.width(24)) register_4 (.D(pc), .en(1'b1), .clk(clk), .Q(pcout), .clr(rst));
  Register #(.width(1)) register_5 (.D(memtoreg), .en(1'b1), .clk(clk), .Q(memtoregout), .clr(rst));
  Register #(.width(1)) register_6 (.D(memwr), .en(1'b1), .clk(clk), .Q(memwrout), .clr(rst));
  Register #(.width(1)) register_7 (.D(regwr), .en(1'b1), .clk(clk), .Q(regwrout), .clr(rst));
  Register #(.width(1)) register_8 (.D(branchneq), .en(1'b1), .clk(clk), .Q(branchneqout), .clr(rst));
  Register #(.width(1)) register_9 (.D(brancheq), .en(1'b1), .clk(clk), .Q(brancheqout), .clr(rst));
  Register #(.width(1)) register_10 (.D(jumpp), .en(1'b1), .clk(clk), .Q(jumppout), .clr(rst));
  Register #(.width(32)) register_11 (.D(ra), .en(1'b1), .clk(clk), .Q(raout), .clr(rst));
  Register #(.width(32)) register_12 (.D(rb), .en(1'b1), .clk(clk), .Q(rbout), .clr(rst));
  Register #(.width(5)) register_13 (.D(rt), .en(1'b1), .clk(clk), .Q(rtout), .clr(rst));
  Register #(.width(5)) register_14 (.D(rd), .en(1'b1), .clk(clk), .Q(rdout), .clr(rst));
  Register #(.width(1)) register_15 (.D(regdest), .en(1'b1), .clk(clk), .Q(regdestout), .clr(rst));
endmodule

module EX_MEM (
  input  [23:0] pc,
  input  [31:0] rb,
  input  memwr,
  input  [31:0] data,
  input  branchEq,
  input  zero,
  input  branchNeq,
  input  memtoreg,
  input  jumpp,
  input  regwr,
  input  clk,
  input  rst,
  input  [4:0] rw,
  input  [23:0] pctest,
  output [23:0] pcout,
  output [31:0] busbout,
  output memwrout,
  output [31:0] dataout,
  output branchEqout,
  output zeroout,
  output branchNeqout,
  output memtoregout,
  output jumppout,
  output regwrout,
  output [4:0] rwout,
  output [23:0] pctestout
);

  Register #(.width(5)) register_1 (.D(rw), .en(1'b1), .clk(clk), .Q(rwout), .clr(rst));
  Register #(.width(24)) register_2 (.D(pc), .en(1'b1), .clk(clk), .Q(pcout), .clr(rst));
  Register #(.width(1)) register_3 (.D(memwr), .en(1'b1), .clk(clk), .Q(memwrout), .clr(rst));
  Register #(.width(1)) register_4 (.D(branchEq), .en(1'b1), .clk(clk), .Q(branchEqout), .clr(rst));
  Register #(.width(1)) register_5 (.D(branchNeq), .en(1'b1), .clk(clk), .Q(branchNeqout), .clr(rst));
  Register #(.width(1)) register_6 (.D(memtoreg), .en(1'b1), .clk(clk), .Q(memtoregout), .clr(rst));
  Register #(.width(1)) register_7 (.D(regwr), .en(1'b1), .clk(clk), .Q(regwrout), .clr(rst));
  Register #(.width(24)) register_8 (.D(pctest), .en(1'b1), .clk(clk), .Q(pctestout), .clr(rst));
  Register #(.width(32)) register_9 (.D(rb), .en(1'b1), .clk(clk), .Q(busbout), .clr(rst));
  Register #(.width(32)) register_10 (.D(data), .en(1'b1), .clk(clk), .Q(dataout), .clr(rst));
  Register #(.width(1)) register_11 (.D(zero), .en(1'b1), .clk(clk), .Q(zeroout), .clr(rst));
  Register #(.width(1)) register_12 (.D(jumpp), .en(1'b1), .clk(clk), .Q(jumppout), .clr(rst));
endmodule

module MEM_WR (
  input  [4:0] rw,
  input  jumpp,
  input  memtoreg,
  input  [31:0] data,
  input  [31:0] dataprev,
  input  regwr,
  input  clk,
  input  rst,
  input  [23:0] pctest,
  output [4:0] rwout,
  output jumppout,
  output memtoregout,
  output [31:0] dataout,
  output [31:0] dataprevout,
  output regwrout,
  output [23:0] pctestout
);

  Register #(.width(24)) register_1 (.D(pctest), .en(1'b1), .clk(clk), .Q(pctestout), .clr(rst));
  Register #(.width(5)) register_2 (.D(rw), .en(1'b1), .clk(clk), .Q(rwout), .clr(rst));
  Register #(.width(1)) register_3 (.D(jumpp), .en(1'b1), .clk(clk), .Q(jumppout), .clr(rst));
  Register #(.width(1)) register_4 (.D(memtoreg), .en(1'b1), .clk(clk), .Q(memtoregout), .clr(rst));
  Register #(.width(32)) register_5 (.D(data), .en(1'b1), .clk(clk), .Q(dataout), .clr(rst));
  Register #(.width(32)) register_6 (.D(dataprev), .en(1'b1), .clk(clk), .Q(dataprevout), .clr(rst));
  Register #(.width(1)) register_7 (.D(regwr), .en(1'b1), .clk(clk), .Q(regwrout), .clr(rst));
endmodule

module Num27Seg (
  input  uno,
  input  dos,
  input  tres,
  input  cuatro,
  output a,
  output b,
  output out_7,
  output d,
  output e,
  output f,
  output g
);

  wire and_1_out, and_2_out, and_3_out, and_4_out, and_5_out, and_6_out, and_7_out, and_8_out, and_9_out,
       and_10_out, and_11_out, and_12_out, and_13_out, and_14_out, and_15_out, and_16_out, and_17_out,
       and_18_out, and_19_out, and_20_out, and_21_out, and_22_out, and_23_out, and_24_out, and_25_out,
       and_26_out, and_27_out, not_1_out, not_2_out, not_3_out, not_4_out, not_5_out, not_6_out, not_7_out,
       not_8_out, not_9_out, not_10_out, not_11_out, not_12_out, not_13_out, not_14_out, not_15_out,
       not_16_out, not_17_out, not_18_out, not_19_out, not_20_out, not_21_out, not_22_out, not_23_out,
       not_24_out, not_25_out, not_26_out, not_27_out, not_28_out, not_29_out, not_30_out, not_31_out,
       not_32_out, not_33_out, not_34_out;

  not not_1 (not_1_out, dos);
  and and_1 (and_1_out, not_1_out, not_2_out);
  not not_2 (not_2_out, cuatro);
  and and_2 (and_2_out, dos, cuatro);
  not not_3 (not_3_out, uno);
  not not_4 (not_4_out, dos);
  not not_5 (not_5_out, uno);
  not not_6 (not_6_out, tres);
  not not_7 (not_7_out, cuatro);
  not not_8 (not_8_out, dos);
  not not_9 (not_9_out, tres);
  not not_10 (not_10_out, uno);
  not not_11 (not_11_out, cuatro);
  not not_12 (not_12_out, uno);
  and and_3 (and_3_out, not_12_out, not_13_out);
  not not_13 (not_13_out, tres);
  not not_14 (not_14_out, dos);
  and and_4 (and_4_out, not_14_out, not_15_out);
  not not_15 (not_15_out, tres);
  not not_16 (not_16_out, uno);
  and and_5 (and_5_out, not_16_out, cuatro);
  and and_6 (and_6_out, dos, tres, not_17_out);
  not not_17 (not_17_out, cuatro);
  not not_18 (not_18_out, dos);
  and and_7 (and_7_out, not_18_out, not_19_out);
  not not_19 (not_19_out, cuatro);
  not not_20 (not_20_out, uno);
  and and_8 (and_8_out, not_20_out, tres, not_21_out);
  not not_21 (not_21_out, cuatro);
  not not_22 (not_22_out, dos);
  and and_9 (and_9_out, not_22_out, tres);
  not not_23 (not_23_out, tres);
  and and_10 (and_10_out, dos, not_23_out, cuatro);
  and and_11 (and_11_out, uno, not_24_out);
  not not_24 (not_24_out, tres);
  and and_12 (and_12_out, uno, cuatro);
  not not_25 (not_25_out, dos);
  and and_13 (and_13_out, not_25_out, not_26_out);
  not not_26 (not_26_out, cuatro);
  and and_14 (and_14_out, tres, not_27_out);
  not not_27 (not_27_out, cuatro);
  and and_15 (and_15_out, uno, tres);
  and and_16 (and_16_out, uno, dos);
  not not_28 (not_28_out, tres);
  and and_17 (and_17_out, not_28_out, not_29_out);
  not not_29 (not_29_out, cuatro);
  and and_18 (and_18_out, dos, not_30_out);
  not not_30 (not_30_out, tres);
  and and_19 (and_19_out, dos, not_31_out);
  not not_31 (not_31_out, cuatro);
  not not_32 (not_32_out, dos);
  and and_20 (and_20_out, not_32_out, tres);
  and and_21 (and_21_out, dos, not_33_out);
  not not_33 (not_33_out, tres);
  and and_22 (and_22_out, dos, not_34_out);
  not not_34 (not_34_out, cuatro);
  or or_1 (a, and_1_out, tres, and_2_out, uno);
  and and_23 (and_23_out, not_3_out, not_4_out);
  and and_24 (and_24_out, not_5_out, not_6_out, not_7_out);
  and and_25 (and_25_out, not_8_out, not_9_out);
  and and_26 (and_26_out, not_10_out, tres, cuatro);
  and and_27 (and_27_out, uno, dos, tres, not_11_out);
  or or_2 (out_7, and_3_out, and_4_out, and_5_out, and_6_out);
  or or_3 (e, and_13_out, and_14_out, and_15_out, and_16_out);
  or or_4 (f, and_17_out, and_18_out, and_19_out, uno);
  or or_5 (g, and_20_out, and_21_out, and_22_out, uno);
  or or_6 (b, and_24_out, and_26_out);
  or or_7 (d, and_7_out, and_8_out, and_9_out, and_10_out, and_11_out, and_12_out);
endmodule

module decodificador (
  input  D,
  input  in_2,
  input  B,
  input  A,
  output out_5,
  output out_6,
  output c,
  output out_8,
  output e,
  output f,
  output g
);

  wire and_1_out, and_2_out, and_3_out, and_4_out, and_5_out, and_6_out, and_7_out, and_8_out, and_9_out,
       and_10_out, and_11_out, and_12_out, and_13_out, and_14_out, and_15_out, and_16_out, and_17_out,
       and_18_out, and_19_out, and_20_out, and_21_out, and_22_out, and_23_out, and_24_out, and_25_out,
       and_26_out, and_27_out, and_28_out, and_29_out, and_30_out, and_31_out, and_32_out, and_33_out,
       and_34_out, and_35_out, and_36_out, and_37_out, and_38_out, and_39_out, and_40_out, not_1_out,
       not_2_out, not_3_out, not_4_out;

  not not_1 (not_1_out, D);
  not not_2 (not_2_out, in_2);
  not not_3 (not_3_out, B);
  not not_4 (not_4_out, A);
  and and_1 (and_1_out, not_2_out, not_4_out);
  and and_2 (and_2_out, not_1_out, B);
  and and_3 (and_3_out, not_1_out, in_2, A);
  and and_4 (and_4_out, D, not_2_out, not_3_out);
  and and_5 (and_5_out, D, not_4_out);
  and and_6 (and_6_out, in_2, B);
  and and_7 (and_7_out, not_1_out, not_3_out, not_4_out);
  and and_8 (and_8_out, not_1_out, B, A);
  and and_9 (and_9_out, not_2_out, not_4_out);
  and and_10 (and_10_out, D, not_3_out, A);
  and and_11 (and_11_out, not_1_out, not_2_out);
  and and_12 (and_12_out, not_1_out, A);
  and and_13 (and_13_out, not_1_out, in_2);
  and and_14 (and_14_out, D, not_2_out, not_4_out);
  and and_15 (and_15_out, not_3_out, A);
  and and_16 (and_16_out, not_1_out, not_3_out);
  and and_17 (and_17_out, in_2, not_3_out, A);
  and and_18 (and_18_out, not_1_out, not_2_out, not_4_out);
  and and_19 (and_19_out, not_1_out, not_2_out, B);
  and and_20 (and_20_out, not_1_out, B, not_4_out);
  and and_21 (and_21_out, not_2_out, not_3_out, not_4_out);
  and and_22 (and_22_out, D, not_3_out);
  and and_23 (and_23_out, not_2_out, B, A);
  and and_24 (and_24_out, in_2, B, not_4_out);
  and and_25 (and_25_out, not_2_out, not_4_out);
  and and_26 (and_26_out, B, not_4_out);
  and and_27 (and_27_out, D, B);
  and and_28 (and_28_out, D, in_2);
  and and_29 (and_29_out, not_3_out, not_4_out);
  and and_30 (and_30_out, not_1_out, in_2, not_3_out);
  and and_31 (and_31_out, in_2, not_4_out);
  and and_32 (and_32_out, D, not_2_out);
  and and_33 (and_33_out, D, B);
  and and_34 (and_34_out, not_2_out, B);
  and and_35 (and_35_out, D, not_2_out);
  and and_36 (and_36_out, not_1_out, in_2, not_3_out);
  and and_37 (and_37_out, not_1_out, in_2, not_4_out);
  and and_38 (and_38_out, in_2, not_3_out, A);
  and and_39 (and_39_out, B, not_4_out);
  and and_40 (and_40_out, D, A);
  or or_1 (out_5, and_1_out, and_2_out, and_3_out, and_4_out, and_5_out, and_6_out);
  or or_2 (out_6, and_7_out, and_8_out, and_9_out, and_10_out, and_11_out);
  or or_3 (c, and_12_out, and_13_out, and_14_out, and_15_out, and_16_out);
  or or_4 (out_8, and_17_out, and_18_out, and_19_out, and_20_out, and_21_out, and_22_out, and_23_out, and_24_out);
  or or_5 (e, and_25_out, and_26_out, and_27_out, and_28_out);
  or or_6 (f, and_29_out, and_30_out, and_31_out, and_32_out, and_33_out);
  or or_7 (g, and_34_out, and_35_out, and_36_out, and_37_out, and_38_out, and_39_out, and_40_out);
endmodule
