// Logisim project Pipeline3.circ as structural Verilog: 16 circuits, main circuit cpu
module upc (
  input  [5:0] opcode,
  output RegDst,
  output ALUSrc,
  output MemtoReg,
  output RegWrite,
  output MemRead,
  output MemWrite,
  output BranchEq,
  output ALUOp1,
  output AluOp0,
  output Jump,
  output BranchNEq
);

  wire and_2_out, and_3_out, and_4_out, not_1_out, not_2_out, not_3_out, not_4_out;

  not not_1 (not_1_out, opcode[3]);
  not not_2 (not_2_out, opcode[2]);
  not not_3 (not_3_out, opcode[1]);
  not not_4 (not_4_out, opcode[0]);
  and and_1 (RegDst, not_1_out, not_3_out);
  and and_2 (and_2_out, not_2_out, opcode[0]);
  and and_3 (and_3_out, not_2_out, not_3_out);
  and and_4 (and_4_out, not_1_out, not_2_out, opcode[0]);
  and and_5 (MemRead, not_1_out, not_2_out, opcode[0]);
  and and_6 (MemWrite, opcode[3], opcode[1]);
  and and_7 (BranchEq, opcode[2], not_4_out);
  and and_8 (ALUOp1, not_1_out, not_2_out, not_3_out);
  and and_9 (Jump, opcode[1], not_4_out);
  and and_10 (BranchNEq, not_3_out, opcode[0]);
  or or_1 (ALUSrc, opcode[3], and_2_out);
  or or_2 (RegWrite, and_3_out, and_4_out);

  assign AluOp0 = opcode[2];
  assign MemtoReg = opcode[0];
endmodule

module cpu (
  output [15:0] out_1,
  output [31:0] out_2,
  output [31:0] out_3,
  output [31:0] out_4,
  output [31:0] out_5,
  output [31:0] out_6,
  output [31:0] out_7,
  output [31:0] out_8,
  output [31:0] out_9,
  output [31:0] out_10,
  output [31:0] out_11,
  output [4:0] SHAMT
);

  wire AluOp0_upc, AluOp1_upc, ALUSrc_upc, AluSrcOut_ID, and_1_out, and_2_out, bne, branch, BranchEq_upc,
       BranchEqOut_ID, BranchNEq_upc, BranchNEqOut_ID, clk, debug_1_add, debug_1_addi, debug_1_an,
       debug_1_beq, debug_1_bne, debug_1_jump, debug_1_load, debug_1_orr, debug_1_store, debug_1_sub,
       debug_2_add, debug_2_addi, debug_2_an, debug_2_beq, debug_2_bne, debug_2_jump, debug_2_load,
       debug_2_orr, debug_2_store, debug_2_sub, debug_3_add, debug_3_addi, debug_3_an, debug_3_beq,
       debug_3_bne, debug_3_jump, debug_3_load, debug_3_orr, debug_3_store, debug_3_sub, debug_4_add,
       debug_4_addi, debug_4_an, debug_4_beq, debug_4_bne, debug_4_jump, debug_4_load, debug_4_orr,
       debug_4_store, debug_4_sub, hazardmanager_1_hayhazard, Jump_upc, jumpOut_EX, JumpOut_ID, jumpp,
       MemRead_upc, MemToReg_upc, memToRegOut_EX, MemToRegOut_ID, MemToRegOut_WR, MemWrite_upc, MemWrOut_ID,
       memWrtOut_EX, not_1_out, not_2_out, or_1_out, RegDestOut_ID, RegDst, RegWrite_upc, regwrmemwr,
       RegWrOut_ID, res, rgwOut_EX, zero, zero_alu;
  wire [1:0] forwardunit_1_forwarda, forwardunit_1_forwardb;
  wire [3:0] AluOpOut_ID, aluOutP_alucontrol;
  wire [4:0] multiplexer_1_out, RC, RD, RdOut_ID, RS, rs_id_ex, RT, RtOut_ID_ID, rwmemwr, RWout_EX;
  wire [5:0] func, func2, func3, func4, opc, opc2, opc3, opc4;
  wire [15:0] ImmOut_ID;
  wire [23:0] adder_2_out, bit_extender_1_out, bit_extender_3_out, bit_extender_4_out, EXMem_PC,
       multiplexer_2_out, multiplexer_5_out, PC, pcexmem, PCout, PCOut_ID, PCtestOut, PCtestOutMemWR,
       register_1_q, subtractor_1_out;
  wire [25:0] jump;
  wire [31:0] alu_d1, alu_d2, bit_extender_2_out, busBOut_EX, busmemwr, dataout_alu, dataout_EX, dataOut_WR,
       dataPrevOut_WR, datoram, if_id_1_instout, memWR_data, multiplexer_3_out, RA_UR, RaOut_ID, RB_UR,
       RbOut_ID;

  Multiplexer #(.width(5)) multiplexer_1 (.in0(RT), .in1(RD), .out(multiplexer_1_out), .sel(RegDst));
  Hex_Digit_Display hex_digit_display_1 (.value(PC[7:4]));  // open: dp
  and and_1 (and_1_out, zero, branch);
  not not_1 (not_1_out, zero);
  and and_2 (and_2_out, not_1_out, bne);
  Hex_Digit_Display hex_digit_display_2 (.value(PC[3:0]));  // open: dp
  Multiplexer #(.width(24)) multiplexer_2 (.in0(PC), .in1(pcexmem), .out(multiplexer_2_out), .sel(or_1_out));
  or or_1 (or_1_out, and_1_out, and_2_out);
  Bit_Extender #(.in_width(26), .out_width(24)) bit_extender_1 (.in(jump), .out(bit_extender_1_out));
  Hex_Digit_Display hex_digit_display_3 (.value(PCout[7:4]));  // open: dp
  Multiplexer #(.select(2), .width(32)) multiplexer_3 (
    .in0(RbOut_ID), .in1(busmemwr), .in2(dataout_EX), .out(multiplexer_3_out), .sel(forwardunit_1_forwardb));  // open: in3
  ForwardUnit forwardunit_1 (
    .Rs(rs_id_ex), .rc_mesa3(RWout_EX), .regwrite_mesa3(rgwOut_EX), .rc_mesa4(rwmemwr), .Rt(RtOut_ID_ID),
    .Rgwrite_mesa_4(regwrmemwr), .ForwardA(forwardunit_1_forwarda), .ForwardB(forwardunit_1_forwardb));
  Hex_Digit_Display hex_digit_display_4 (.value(PCout[3:0]));  // open: dp
  debug debug_1 (
    .opcode(opc), .functioncode(func), .ADD(debug_1_add), .SUB(debug_1_sub), .AN(debug_1_an),
    .ORR(debug_1_orr), .ADDI(debug_1_addi), .LOAD(debug_1_load), .STORE(debug_1_store), .BEQ(debug_1_beq),
    .BNE(debug_1_bne), .JUMP(debug_1_jump));
  Multiplexer #(.select(2), .width(32)) multiplexer_4 (
    .in0(RaOut_ID), .in1(busmemwr), .in2(dataout_EX), .out(alu_d1), .sel(forwardunit_1_forwarda));  // open: in3
  Register #(.width(24)) register_1 (.D(multiplexer_5_out), .clk(clk), .Q(register_1_q), .clr(res));  // open: en
  Multiplexer #(.width(24)) multiplexer_5 (
    .in0(multiplexer_2_out), .in1(bit_extender_1_out), .out(multiplexer_5_out), .sel(jumpp));
  not not_2 (not_2_out, hazardmanager_1_hayhazard);
  HazardManager hazardmanager_1 (
    .clk(clk), .inst(datoram), .rc2(multiplexer_1_out), .rc3(RC), .opcode2(opc), .opcode3(opc2),
    .HayHazard(hazardmanager_1_hayhazard));
  LED led_1 (.in(debug_1_add));
  LED led_2 (.in(debug_1_sub));
  LED led_3 (.in(debug_1_an));
  LED led_4 (.in(debug_1_orr));
  LED led_5 (.in(debug_1_addi));
  LED led_6 (.in(debug_1_load));
  LED led_7 (.in(debug_1_store));
  LED led_8 (.in(debug_1_beq));
  LED led_9 (.in(debug_1_bne));
  LED led_10 (.in(debug_1_jump));
  assign bit_extender_2_out = {{16{ImmOut_ID[15]}}, ImmOut_ID};  // Bit_Extender bit_extender_2
  Multiplexer #(.width(32)) multiplexer_6 (
    .in0(multiplexer_3_out), .in1(bit_extender_2_out), .out(alu_d2), .sel(AluSrcOut_ID));
  Adder #(.width(24)) adder_1 (.a(24'h1), .b(register_1_q), .out(PC));  // open: cin, cout
  RAM #(.addrWidth(24), .dataWidth(32), .enables("line")) ram_1 (
    .addr(register_1_q), .clk(clk), .dout(datoram));  // open: we, din
  Button button_1 (.out(res));
  Clock clock_1 (.out(clk));
  Hex_Digit_Display hex_digit_display_5 (.value(PCOut_ID[7:4]));  // open: dp
  Hex_Digit_Display hex_digit_display_6 (.value(PCOut_ID[3:0]));  // open: dp
  debug debug_2 (
    .opcode(opc2), .functioncode(func2), .ADD(debug_2_add), .SUB(debug_2_sub), .AN(debug_2_an),
    .ORR(debug_2_orr), .ADDI(debug_2_addi), .LOAD(debug_2_load), .STORE(debug_2_store), .BEQ(debug_2_beq),
    .BNE(debug_2_bne), .JUMP(debug_2_jump));
  LED led_11 (.in(debug_2_add));
  LED led_12 (.in(debug_2_sub));
  LED led_13 (.in(debug_2_an));
  LED led_14 (.in(debug_2_orr));
  LED led_15 (.in(debug_2_addi));
  LED led_16 (.in(debug_2_load));
  LED led_17 (.in(debug_2_store));
  LED led_18 (.in(debug_2_beq));
  LED led_19 (.in(debug_2_bne));
  LED led_20 (.in(debug_2_jump));
  Hex_Digit_Display hex_digit_display_7 (.value(PCtestOut[7:4]));  // open: dp
  assign bit_extender_3_out = {{9{ImmOut_ID[14]}}, ImmOut_ID[14:0]};  // Bit_Extender bit_extender_3
  Hex_Digit_Display hex_digit_display_8 (.value(PCtestOut[3:0]));  // open: dp
  debug debug_3 (
    .opcode(opc3), .functioncode(func3), .ADD(debug_3_add), .SUB(debug_3_sub), .AN(debug_3_an),
    .ORR(debug_3_orr), .ADDI(debug_3_addi), .LOAD(debug_3_load), .STORE(debug_3_store), .BEQ(debug_3_beq),
    .BNE(debug_3_bne), .JUMP(debug_3_jump));
  Adder #(.width(24)) adder_2 (.a(PCOut_ID), .b(bit_extender_3_out), .out(adder_2_out));  // open: cin, cout
  Subtractor #(.width(24)) subtractor_1 (
    .a(PCOut_ID), .b(bit_extender_3_out), .out(subtractor_1_out));  // open: bin, bout
  alu alu_1 (.d1(alu_d1), .d2(alu_d2), .Aluop(AluOpOut_ID), .dataout(dataout_alu), .zero(zero_alu));
  Multiplexer #(.width(24)) multiplexer_7 (
    .in0(adder_2_out), .in1(subtractor_1_out), .out(EXMem_PC), .sel(ImmOut_ID[15]));
  LED led_21 (.in(debug_3_add));
  LED led_22 (.in(debug_3_sub));
  LED led_23 (.in(debug_3_an));
  LED led_24 (.in(debug_3_orr));
  LED led_25 (.in(debug_3_addi));
  LED led_26 (.in(debug_3_load));
  LED led_27 (.in(debug_3_store));
  LED led_28 (.in(debug_3_beq));
  LED led_29 (.in(debug_3_bne));
  LED led_30 (.in(debug_3_jump));
  Multiplexer #(.width(5)) multiplexer_8 (.in0(RtOut_ID_ID), .in1(RdOut_ID), .out(RC), .sel(RegDestOut_ID));
  EX_MEM ex_mem_1 (
    .func(func2), .opc(opc2), .pc(EXMem_PC), .rb(RbOut_ID), .memwr(MemWrOut_ID), .data(dataout_alu),
    .branchEq(BranchEqOut_ID), .zero(zero_alu), .branchNeq(BranchNEqOut_ID), .memtoreg(MemToRegOut_ID),
    .jumpp(JumpOut_ID), .regwr(RegWrOut_ID), .clk(clk), .rw(RC), .rst(res), .pctest(PCOut_ID),
    .funcout(func3), .opcout(opc3), .pcout(pcexmem), .busbout(busBOut_EX), .memwrout(memWrtOut_EX),
    .dataout(dataout_EX), .branchEqout(branch), .zeroout(zero), .branchNeqout(bne),
    .memtoregout(memToRegOut_EX), .jumppout(jumpOut_EX), .regwrout(rgwOut_EX), .rwout(RWout_EX),
    .pctestout(PCtestOut));
  Hex_Digit_Display hex_digit_display_9 (.value(PCtestOutMemWR[7:4]));  // open: dp
  Hex_Digit_Display hex_digit_display_10 (.value(PCtestOutMemWR[3:0]));  // open: dp
  debug debug_4 (
    .opcode(opc4), .functioncode(func4), .ADD(debug_4_add), .SUB(debug_4_sub), .AN(debug_4_an),
    .ORR(debug_4_orr), .ADDI(debug_4_addi), .LOAD(debug_4_load), .STORE(debug_4_store), .BEQ(debug_4_beq),
    .BNE(debug_4_bne), .JUMP(debug_4_jump));
  LED led_31 (.in(debug_4_add));
  LED led_32 (.in(debug_4_sub));
  LED led_33 (.in(debug_4_an));
  LED led_34 (.in(debug_4_orr));
  LED led_35 (.in(debug_4_addi));
  LED led_36 (.in(debug_4_load));
  LED led_37 (.in(debug_4_store));
  LED led_38 (.in(debug_4_beq));
  LED led_39 (.in(debug_4_bne));
  LED led_40 (.in(debug_4_jump));
  IF_ID if_id_1 (
    .inst(datoram), .pc(PC), .clk(clk), .reset(res), .HayHazard(1'b0), .instout(if_id_1_instout),
    .pcout(PCout));
  Spliter spliter_1 (
    .ENTRADA(if_id_1_instout), .rt(RT), .funct(func), .sham(SHAMT), .opcode(opc), .rd(RD), .rs(RS),
    .off(out_1), .jump(jump));
  UR ur_1 (
    .clk(clk), .data(busmemwr), .rst(res), .regw(regwrmemwr), .rw(rwmemwr), .ra(RS), .rb(RT), .r8_t0(out_2),
    .r9_t1(out_3), .r10_t2(out_4), .r11_t3(out_5), .r12_t4(out_6), .r13_t5(out_7), .r14_t6(out_8),
    .r15_t7(out_9), .Rra(RA_UR), .Rrb(RB_UR), .r24_t7(out_10), .r25_t8(out_11));
  upc upc_1 (
    .opcode(opc), .RegDst(RegDst), .ALUSrc(ALUSrc_upc), .MemtoReg(MemToReg_upc), .RegWrite(RegWrite_upc),
    .MemRead(MemRead_upc), .MemWrite(MemWrite_upc), .BranchEq(BranchEq_upc), .ALUOp1(AluOp1_upc),
    .AluOp0(AluOp0_upc), .Jump(Jump_upc), .BranchNEq(BranchNEq_upc));
  alucontrol alucontrol_1 (.aluop({AluOp1_upc, AluOp0_upc}), .funct(func), .aluopout(aluOutP_alucontrol));
  ID_EX id_ex_1 (
    .rs(RS), .func(func), .opc(opc), .alusrc(ALUSrc_upc), .aluop(aluOutP_alucontrol), .imm(out_1),
    .memwr(MemWrite_upc), .pc(PCout), .regwr(RegWrite_upc), .memtoreg(MemToReg_upc),
    .branchneq(BranchNEq_upc), .clk(clk), .brancheq(BranchEq_upc), .rst(res), .jumpp(Jump_upc), .ra(RA_UR),
    .rb(RB_UR), .rt(RT), .rd(RD), .regdest(RegDst), .rsout(rs_id_ex), .funcout(func2), .opcout(opc2),
    .alusrcout(AluSrcOut_ID), .aluopout(AluOpOut_ID), .immout(ImmOut_ID), .memwrout(MemWrOut_ID),
    .pcout(PCOut_ID), .regwrout(RegWrOut_ID), .memtoregout(MemToRegOut_ID), .branchneqout(BranchNEqOut_ID),
    .brancheqout(BranchEqOut_ID), .jumppout(JumpOut_ID), .raout(RaOut_ID), .rbout(RbOut_ID),
    .rtout(RtOut_ID_ID), .rdout(RdOut_ID), .regdestout(RegDestOut_ID));
  Bit_Extender #(.in_width(32), .out_width(24)) bit_extender_4 (.in(dataout_EX), .out(bit_extender_4_out));
  Multiplexer #(.width(32)) multiplexer_9 (
    .in0(dataPrevOut_WR), .in1(dataOut_WR), .out(busmemwr), .sel(MemToRegOut_WR));
  RAM #(.addrWidth(24), .dataWidth(32), .enables("line")) ram_2 (
    .addr(bit_extender_4_out), .we(memWrtOut_EX), .clk(clk), .din(busBOut_EX), .dout(memWR_data));
  MEM_WR mem_wr_1 (
    .func(func3), .opc(opc3), .rw(RWout_EX), .jumpp(jumpOut_EX), .memtoreg(memToRegOut_EX),
    .data(memWR_data), .dataprev(dataout_EX), .regwr(rgwOut_EX), .clk(clk), .rst(res), .pctest(PCtestOut),
    .funcout(func4), .opcout(opc4), .rwout(rwmemwr), .jumppout(jumpp), .memtoregout(MemToRegOut_WR),
    .dataout(dataOut_WR), .dataprevout(dataPrevOut_WR), .regwrout(regwrmemwr), .pctestout(PCtestOutMemWR));

  // Other names for the same wires on the sheet: imm[15:0] = out_1; t0[31:0] = out_2; t1[31:0] = out_3;
  //   t2[31:0] = out_4; t3[31:0] = out_5; t4[31:0] = out_6; t5[31:0] = out_7; t6[31:0] = out_8; t7[31:0] = out_9;
  //   t8[31:0] = out_10; t9[31:0] = out_11
endmodule

module Spliter (
  input  [31:0] ENTRADA,
  output [4:0] rt,
  output [5:0] funct,
  output [4:0] sham,
  output [5:0] opcode,
  output [4:0] rd,
  output [4:0] rs,
  output [15:0] off,
  output [25:0] jump
);


  assign funct = ENTRADA[5:0];
  assign jump = ENTRADA[25:0];
  assign off = ENTRADA[15:0];
  assign opcode = ENTRADA[31:26];
  assign rd = ENTRADA[15:11];
  assign rs = ENTRADA[25:21];
  assign rt = ENTRADA[20:16];
  assign sham = ENTRADA[10:6];
endmodule

module alucontrol (
  input  [1:0] aluop,
  input  [5:0] funct,
  output [3:0] aluopout
);

  wire not_1_out, not_2_out, or_1_out, or_2_out, or_4_out;

  not not_1 (not_1_out, aluop[1]);
  not not_2 (not_2_out, funct[2]);
  or or_1 (or_1_out, aluop[1], aluop[0]);
  or or_2 (or_2_out, aluop[0], funct[1]);
  or or_3 (aluopout[1], not_1_out, not_2_out);
  or or_4 (or_4_out, funct[3], funct[0]);
  and and_1 (aluopout[2], or_1_out, or_2_out);
  and and_2 (aluopout[0], aluop[1], or_4_out);

  assign aluopout[3] = 1'b1;
endmodule

module debug (
  input  [5:0] opcode,
  input  [5:0] functioncode,
  output ADD,
  output SUB,
  output AN,
  output ORR,
  output ADDI,
  output LOAD,
  output STORE,
  output BEQ,
  output BNE,
  output JUMP
);

  wire not_1_out, not_2_out, not_3_out, not_4_out, not_5_out, not_6_out, not_7_out, not_8_out;

  not not_1 (not_1_out, opcode[5]);
  not not_2 (not_2_out, opcode[3]);
  not not_3 (not_3_out, opcode[2]);
  not not_4 (not_4_out, opcode[1]);
  not not_5 (not_5_out, opcode[0]);
  not not_6 (not_6_out, functioncode[2]);
  not not_7 (not_7_out, functioncode[1]);
  not not_8 (not_8_out, functioncode[0]);
  and and_1 (ADD, not_2_out, not_3_out, not_4_out, not_6_out, not_7_out);
  and and_2 (SUB, not_2_out, not_3_out, not_4_out, functioncode[1]);
  and and_3 (AN, not_2_out, not_3_out, not_4_out, functioncode[2], not_8_out);
  and and_4 (ORR, not_2_out, not_3_out, not_4_out, functioncode[0]);
  and and_5 (ADDI, opcode[3], not_4_out);
  and and_6 (LOAD, not_2_out, not_3_out, opcode[0]);
  and and_7 (STORE, opcode[3], opcode[0]);
  and and_8 (BEQ, opcode[2], not_5_out);
  and and_9 (BNE, not_4_out, opcode[0]);
  and and_10 (JUMP, not_1_out, opcode[1]);
endmodule

module UR (
  input  clk,
  input  [31:0] data,
  input  rst,
  input  regw,
  input  [4:0] rw,
  input  [4:0] ra,
  input  [4:0] rb,
  output [31:0] r8_t0,
  output [31:0] r9_t1,
  output [31:0] r10_t2,
  output [31:0] r11_t3,
  output [31:0] r12_t4,
  output [31:0] r13_t5,
  output [31:0] r14_t6,
  output [31:0] r15_t7,
  output [31:0] Rra,
  output [31:0] Rrb,
  output [31:0] r24_t7,
  output [31:0] r25_t8
);

  wire R0W, R1W, R2W, R3W, R4W, R5W, R6W, R7W, R8W, R9W, R10W, R11W, R12W, R13W, R14W, R15W, R16W, R17W,
       R18W, R19W, R20W, R21W, R22W, R23W, R24W, R25W, R26W, R27W, R28W, R29W, R30W, R31W;
  wire [31:0] R0, R1, R2, R3, R4, R5, R6, R7, R16, R17, R18, R19, R20, R21, R22, R23, R26, R27, R28, R29,
       R30, R31;

  Register #(.width(32)) register_1 (.D(data), .en(R0W), .Q(R0), .clk(clk), .clr(rst));
  Register #(.width(32)) register_2 (.D(data), .en(R8W), .Q(r8_t0), .clk(clk), .clr(rst));
  Register #(.width(32)) register_3 (.D(data), .en(R16W), .Q(R16), .clk(clk), .clr(rst));
  Register #(.width(32)) register_4 (.D(data), .en(R24W), .Q(r24_t7), .clk(clk), .clr(rst));
  Register #(.width(32)) register_5 (.D(data), .en(R1W), .Q(R1), .clk(clk), .clr(rst));
  Register #(.width(32)) register_6 (.D(data), .en(R9W), .Q(r9_t1), .clk(clk), .clr(rst));
  Register #(.width(32)) register_7 (.D(data), .en(R17W), .Q(R17), .clk(clk), .clr(rst));
  Register #(.width(32)) register_8 (.D(data), .en(R25W), .Q(r25_t8), .clk(clk), .clr(rst));
  Multiplexer #(.select(5), .width(32)) multiplexer_1 (
    .in0(R0), .in1(R1), .in2(R2), .in3(R3), .in4(R4), .in5(R5), .in6(R6), .in7(R7), .in8(r8_t0), .in9(r9_t1),
    .in10(r10_t2), .in11(r11_t3), .in12(r12_t4), .in13(r13_t5), .in14(r14_t6), .in15(r15_t7), .in16(R16),
    .in17(R17), .in18(R18), .in19(R19), .in20(R20), .in21(R21), .in22(R22), .in23(R23), .in24(r24_t7),
    .in25(r25_t8), .in26(R26), .in27(R27), .in28(R28), .in29(R29), .in30(R30), .in31(R31), .out(Rra), .sel(ra));
  Register #(.width(32)) register_9 (.D(data), .en(R10W), .Q(r10_t2), .clk(clk), .clr(rst));
  Register #(.width(32)) register_10 (.D(data), .en(R18W), .Q(R18), .clk(clk), .clr(rst));
  Register #(.width(32)) register_11 (.D(data), .en(R26W), .Q(R26), .clk(clk), .clr(rst));
  Register #(.width(32)) register_12 (.D(data), .en(R2W), .Q(R2), .clk(clk), .clr(rst));
  Register #(.width(32)) register_13 (.D(data), .en(R11W), .Q(r11_t3), .clk(clk), .clr(rst));
  Register #(.width(32)) register_14 (.D(data), .en(R19W), .Q(R19), .clk(clk), .clr(rst));
  Register #(.width(32)) register_15 (.D(data), .en(R3W), .Q(R3), .clk(clk), .clr(rst));
  Register #(.width(32)) register_16 (.D(data), .en(R27W), .Q(R27), .clk(clk), .clr(rst));
  Multiplexer #(.select(5), .width(32)) multiplexer_2 (
    .in0(R0), .in1(R1), .in2(R2), .in3(R3), .in4(R4), .in5(R5), .in6(R6), .in7(R7), .in8(r8_t0), .in9(r9_t1),
    .in10(r10_t2), .in11(r11_t3), .in12(r12_t4), .in13(r13_t5), .in14(r14_t6), .in15(r15_t7), .in16(R16),
    .in17(R17), .in18(R18), .in19(R19), .in20(R20), .in21(R21), .in22(R22), .in23(R23), .in24(r24_t7),
    .in25(r25_t8), .in26(R26), .in27(R27), .in28(R28), .in29(R29), .in30(R30), .in31(R31), .out(Rrb), .sel(rb));
  Register #(.width(32)) register_17 (.D(data), .en(R4W), .Q(R4), .clk(clk), .clr(rst));
  Register #(.width(32)) register_18 (.D(data), .en(R12W), .Q(r12_t4), .clk(clk), .clr(rst));
  Register #(.width(32)) register_19 (.D(data), .en(R20W), .Q(R20), .clk(clk), .clr(rst));
  Register #(.width(32)) register_20 (.D(data), .en(R28W), .Q(R28), .clk(clk), .clr(rst));
  Register #(.width(32)) register_21 (.D(data), .en(R5W), .Q(R5), .clk(clk), .clr(rst));
  Register #(.width(32)) register_22 (.D(data), .en(R13W), .Q(r13_t5), .clk(clk), .clr(rst));
  Register #(.width(32)) register_23 (.D(data), .en(R21W), .Q(R21), .clk(clk), .clr(rst));
  Register #(.width(32)) register_24 (.D(data), .en(R29W), .Q(R29), .clk(clk), .clr(rst));
  Register #(.width(32)) register_25 (.D(data), .en(R6W), .Q(R6), .clk(clk), .clr(rst));
  Register #(.width(32)) register_26 (.D(data), .en(R14W), .Q(r14_t6), .clk(clk), .clr(rst));
  Register #(.width(32)) register_27 (.D(data), .en(R22W), .Q(R22), .clk(clk), .clr(rst));
  Register #(.width(32)) register_28 (.D(data), .en(R30W), .Q(R30), .clk(clk), .clr(rst));
  Demultiplexer #(.select(5)) demultiplexer_1 (
    .out0(R0W), .out1(R1W), .out2(R2W), .out3(R3W), .out4(R4W), .out5(R5W), .out6(R6W), .out7(R7W),
    .out8(R8W), .out9(R9W), .out10(R10W), .out11(R11W), .out12(R12W), .out13(R13W), .out14(R14W),
    .out15(R15W), .out16(R16W), .out17(R17W), .out18(R18W), .out19(R19W), .out20(R20W), .out21(R21W),
    .out22(R22W), .out23(R23W), .out24(R24W), .out25(R25W), .out26(R26W), .out27(R27W), .out28(R28W),
    .out29(R29W), .out30(R30W), .out31(R31W), .in(regw), .sel(rw));
  Register #(.width(32)) register_29 (.D(data), .en(R15W), .Q(r15_t7), .clk(clk), .clr(rst));
  Register #(.width(32)) register_30 (.D(data), .en(R23W), .Q(R23), .clk(clk), .clr(rst));
  Register #(.width(32)) register_31 (.D(data), .en(R31W), .Q(R31), .clk(clk), .clr(rst));
  Register #(.width(32)) register_32 (.D(data), .en(R7W), .Q(R7), .clk(clk), .clr(rst));

  // Other names for the same wires on the sheet: R8[31:0] = r8_t0; R9[31:0] = r9_t1; R10[31:0] = r10_t2;
  //   R11[31:0] = r11_t3; R12[31:0] = r12_t4; R13[31:0] = r13_t5; R14[31:0] = r14_t6; R15[31:0] = r15_t7;
  //   R24[31:0] = r24_t7; R25[31:0] = r25_t8
endmodule

module alu (
  input  [31:0] d1,
  input  [31:0] d2,
  input  [3:0] Aluop,
  output [31:0] dataout,
  output zero
);

  wire [31:0] addd, andd, orr, subb;

  assign andd = d1 & d2;  // AND_Gate and_1, 32 bits wide
  assign orr = d1 | d2;  // OR_Gate or_1, 32 bits wide
  Adder #(.width(32)) adder_1 (.a(d1), .b(d2), .out(addd));  // open: cin, cout
  Subtractor #(.width(32)) subtractor_1 (.a(d1), .b(d2), .out(subb));  // open: bin, bout
  Multiplexer #(.select(4), .width(32)) multiplexer_1 (
    .in8(andd), .in9(orr), .in10(addd), .in14(subb), .out(dataout), .sel(Aluop));  // open: in0, in1, in2, in3, in4, in5, in6, in7, in11, in12, in13, in15
  Comparator #(.width(32)) comparator_1 (.a(dataout), .b({32{1'b0}}), .eq(zero));  // open: gt, lt
endmodule

module IF_ID (
  input  [31:0] inst,
  input  [23:0] pc,
  input  clk,
  input  reset,
  input  HayHazard,
  output [31:0] instout,
  output [23:0] pcout
);

  wire [31:0] multiplexer_1_out;

  Multiplexer #(.width(32)) multiplexer_1 (.in0(inst), .in1({32{1'b0}}), .out(multiplexer_1_out), .sel(HayHazard));
  Register #(.width(32)) register_1 (.D(multiplexer_1_out), .en(1'b1), .clk(clk), .Q(instout), .clr(reset));
  Register #(.width(24)) register_2 (.D(pc), .en(1'b1), .clk(clk), .Q(pcout), .clr(reset));
endmodule

module ID_EX (
  input  [4:0] rs,
  input  [5:0] func,
  input  [5:0] opc,
  input  alusrc,
  input  [3:0] aluop,
  input  [15:0] imm,
  input  memwr,
  input  [23:0] pc,
  input  regwr,
  input  memtoreg,
  input  branchneq,
  input  clk,
  input  brancheq,
  input  rst,
  input  jumpp,
  input  [31:0] ra,
  input  [31:0] rb,
  input  [4:0] rt,
  input  [4:0] rd,
  input  regdest,
  output [4:0] rsout,
  output [5:0] funcout,
  output [5:0] opcout,
  output alusrcout,
  output [3:0] aluopout,
  output [15:0] immout,
  output memwrout,
  output [23:0] pcout,
  output regwrout,
  output memtoregout,
  output branchneqout,
  output brancheqout,
  output jumppout,
  output [31:0] raout,
  output [31:0] rbout,
  output [4:0] rtout,
  output [4:0] rdout,
  output regdestout
);

  Register #(.width(5)) register_1 (.D(rs), .en(1'b1), .clk(clk), .Q(rsout), .clr(rst));
  Register #(.width(6)) register_2 (.D(func), .en(1'b1), .clk(clk), .Q(funcout), .clr(rst));
  Register #(.width(6)) register_3 (.D(opc), .en(1'b1), .clk(clk), .Q(opcout), .clr(rst));
  Register #(.width(1)) register_4 (.D(alusrc), .en(1'b1), .clk(clk), .Q(alusrcout), .clr(rst));
  Register #(.width(4)) register_5 (.D(aluop), .en(1'b1), .clk(clk), .Q(aluopout), .clr(rst));
  Register #(.width(16)) register_6 (.D(imm), .en(1'b1), .clk(clk), .Q(immout), .clr(rst));
  Register #(.width(24)) register_7 (.D(pc), .en(1'b1), .clk(clk), .Q(pcout), .clr(rst));
  Register #(.width(1)) register_8 (.D(memtoreg), .en(1'b1), .clk(clk), .Q(memtoregout), .clr(rst));
  Register #(.width(1)) register_9 (.D(memwr), .en(1'b1), .clk(clk), .Q(memwrout), .clr(rst));
  Register #(.width(1)) register_10 (.D(regwr), .en(1'b1), .clk(clk), .Q(regwrout), .clr(rst));
  Register #(.width(1)) register_11 (.D(branchneq), .en(1'b1), .clk(clk), .Q(branchneqout), .clr(rst));
  Register #(.width(1)) register_12 (.D(brancheq), .en(1'b1), .clk(clk), .Q(brancheqout), .clr(rst));
  Register #(.width(1)) register_13 (.D(jumpp), .en(1'b1), .clk(clk), .Q(jumppout), .clr(rst));
  Register #(.width(32)) register_14 (.D(ra), .en(1'b1), .clk(clk), .Q(raout), .clr(rst));
  Register #(.width(32)) register_15 (.D(rb), .en(1'b1), .clk(clk), .Q(rbout), .clr(rst));
  Register #(.width(5)) register_16 (.D(rt), .en(1'b1), .clk(clk), .Q(rtout), .clr(rst));
  Register #(.width(5)) register_17 (.D(rd), .en(1'b1), .clk(clk), .Q(rdout), .clr(rst));
  Register #(.width(1)) register_18 (.D(regdest), .en(1'b1), .clk(clk), .Q(regdestout), .clr(rst));
endmodule

module EX_MEM (
  input  [5:0] func,
  input  [5:0] opc,
  input  [23:0] pc,
  input  [31:0] rb,
  input  memwr,
  input  [31:0] data,
  input  branchEq,
  input  zero,
  input  branchNeq,
  input  memtoreg,
  input  jumpp,
  input  regwr,
  input  clk,
  input  [4:0] rw,
  input  rst,
  input  [23:0] pctest,
  output [5:0] funcout,
  output [5:0] opcout,
  output [23:0] pcout,
  output [31:0] busbout,
  output memwrout,
  output [31:0] dataout,
  output branchEqout,
  output zeroout,
  output branchNeqout,
  output memtoregout,
  output jumppout,
  output regwrout,
  output [4:0] rwout,
  output [23:0] pctestout
);

  Register #(.width(6)) register_1 (.D(func), .en(1'b1), .clk(clk), .Q(funcout), .clr(rst));
  Register #(.width(5)) register_2 (.D(rw), .en(1'b1), .clk(clk), .Q(rwout), .clr(rst));
  Register #(.width(24)) register_3 (.D(pctest), .en(1'b1), .clk(clk), .Q(pctestout), .clr(rst));
  Register #(.width(24)) register_4 (.D(pc), .en(1'b1), .clk(clk), .Q(pcout), .clr(rst));
  Register #(.width(1)) register_5 (.D(memwr), .en(1'b1), .clk(clk), .Q(memwrout), .clr(rst));
  Register #(.width(1)) register_6 (.D(branchEq), .en(1'b1), .clk(clk), .Q(branchEqout), .clr(rst));
  Register #(.width(1)) register_7 (.D(branchNeq), .en(1'b1), .clk(clk), .Q(branchNeqout), .clr(rst));
  Register #(.width(1)) register_8 (.D(memtoreg), .en(1'b1), .clk(clk), .Q(memtoregout), .clr(rst));
  Register #(.width(1)) register_9 (.D(regwr), .en(1'b1), .clk(clk), .Q(regwrout), .clr(rst));
  Register #(.width(6)) register_10 (.D(opc), .en(1'b1), .clk(clk), .Q(opcout), .clr(rst));
  Register #(.width(32)) register_11 (.D(rb), .en(1'b1), .clk(clk), .Q(busbout), .clr(rst));
  Register #(.width(32)) register_12 (.D(data), .en(1'b1), .clk(clk), .Q(dataout), .clr(rst));
  Register #(.width(1)) register_13 (.D(zero), .en(1'b1), .clk(clk), .Q(zeroout), .clr(rst));
  Register #(.width(1)) register_14 (.D(jumpp), .en(1'b1), .clk(clk), .Q(jumppout), .clr(rst));
endmodule

module MEM_WR (
  input  [5:0] func,
  input  [5:0] opc,
  input  [4:0] rw,
  input  jumpp,
  input  memtoreg,
  input  [31:0] data,
  input  [31:0] dataprev,
  input  regwr,
  input  clk,
  input  rst,
  input  [23:0] pctest,
  output [5:0] funcout,
  output [5:0] opcout,
  output [4:0] rwout,
  output jumppout,
  output memtoregout,
  output [31:0] dataout,
  output [31:0] dataprevout,
  output regwrout,
  output [23:0] pctestout
);

  Register #(.width(6)) register_1 (.D(func), .en(1'b1), .clk(clk), .Q(funcout), .clr(rst));
  Register #(.width(6)) register_2 (.D(opc), .en(1'b1), .clk(clk), .Q(opcout), .clr(rst));
  Register #(.width(5)) register_3 (.D(rw), .en(1'b1), .clk(clk), .Q(rwout), .clr(rst));
  Register #(.width(1)) register_4 (.D(jumpp), .en(1'b1), .clk(clk), .Q(jumppout), .clr(rst));
  Register #(.width(1)) register_5 (.D(memtoreg), .en(1'b1), .clk(clk), .Q(memtoregout), .clr(rst));
  Register #(.width(32)) register_6 (.D(data), .en(1'b1), .clk(clk), .Q(dataout), .clr(rst));
  Register #(.width(32)) register_7 (.D(dataprev), .en(1'b1), .clk(clk), .Q(dataprevout), .clr(rst));
  Register #(.width(1)) register_8 (.D(regwr), .en(1'b1), .clk(clk), .Q(regwrout), .clr(rst));
  Register #(.width(24)) register_9 (.D(pctest), .en(1'b1), .clk(clk), .Q(pctestout), .clr(rst));
endmodule

module HazardHandler (
  input  [5:0] opcode1,
  input  [5:0] opcode2,
  input  [4:0] rt,
  input  [4:0] rc,
  input  [4:0] rs,
  output hazardout
);

  wire and_1_out, comparator_1_eq, comparator_2_eq, comparator_3_eq, comparator_4_eq, comparator_5_eq,
       comparator_7_eq, comparator_8_eq, multiplexer_1_out, muxx, or_1_out, or_2_out, or_3_out;

  Comparator #(.width(6)) comparator_1 (.a(opcode1), .b({6{1'b0}}), .eq(comparator_1_eq));  // open: gt, lt
  Comparator #(.width(6)) comparator_2 (.a(opcode1), .b(6'b100011), .eq(comparator_2_eq));  // open: gt, lt
  Comparator #(.width(6)) comparator_3 (.a(opcode1), .b(6'b001000), .eq(comparator_3_eq));  // open: gt, lt
  Comparator #(.width(6)) comparator_4 (.a(opcode2), .b({6{1'b0}}), .eq(comparator_4_eq));  // open: gt, lt
  Comparator #(.width(6)) comparator_5 (.a(opcode2), .b(6'b101011), .eq(comparator_5_eq));  // open: gt, lt
  Comparator #(.width(6)) comparator_6 (.a(opcode2), .b(6'b001000), .eq(muxx));  // open: gt, lt
  Comparator #(.width(5)) comparator_7 (.a(rc), .b(rt), .eq(comparator_7_eq));  // open: gt, lt
  Comparator #(.width(5)) comparator_8 (.a(rc), .b(rs), .eq(comparator_8_eq));  // open: gt, lt
  or or_1 (or_1_out, comparator_7_eq, comparator_8_eq);
  or or_2 (or_2_out, comparator_1_eq, comparator_2_eq, comparator_3_eq);
  or or_3 (or_3_out, comparator_4_eq, comparator_5_eq, muxx);
  Multiplexer multiplexer_1 (.in0(or_1_out), .in1(comparator_8_eq), .out(multiplexer_1_out), .sel(muxx));
  and and_1 (and_1_out, or_2_out, or_3_out);
  and and_2 (hazardout, and_1_out, multiplexer_1_out);
endmodule

module HazardResolver (
  input  hazardin2,
  input  clk,
  input  hazardin,
  output out_4
);

  wire and_1_out, and_2_out, and_3_out, and_5_out, multiplexer_1_out, not_1_out, not_2_out, not_3_out,
       not_4_out, not_5_out, not_6_out, or_1_out, or_2_out, register_1_q, subtractor_1_out;
  wire [1:0] multiplexer_2_out, register_2_q, subtractor_2_out;

  not not_1 (not_1_out, and_2_out);
  and and_1 (and_1_out, not_1_out, subtractor_1_out);
  not not_2 (not_2_out, subtractor_1_out);
  not not_3 (not_3_out, not_2_out);
  and and_2 (and_2_out, not_3_out, hazardin);
  and and_3 (and_3_out, not_4_out, subtractor_2_out[1]);
  not not_4 (not_4_out, and_5_out);
  Multiplexer multiplexer_1 (.in0(subtractor_1_out), .in1(hazardin), .out(multiplexer_1_out), .sel(and_2_out));
  or or_1 (or_1_out, not_2_out, and_2_out);
  and and_4 (out_4, and_1_out, and_3_out);
  not not_5 (not_5_out, subtractor_2_out[1]);
  not not_6 (not_6_out, not_5_out);
  and and_5 (and_5_out, not_6_out, hazardin2);
  Register #(.width(1)) register_1 (.D(multiplexer_1_out), .en(or_1_out), .clk(clk), .Q(register_1_q));  // open: clr
  Multiplexer #(.width(2)) multiplexer_2 (
    .in0(subtractor_2_out), .in1({hazardin2, 1'b0}), .out(multiplexer_2_out), .sel(and_5_out));
  or or_2 (or_2_out, not_5_out, and_5_out);
  Subtractor #(.width(1)) subtractor_1 (.a(register_1_q), .b(1'b1), .out(subtractor_1_out));  // open: bin, bout
  Register #(.width(2)) register_2 (.D(multiplexer_2_out), .en(or_2_out), .clk(clk), .Q(register_2_q));  // open: clr
  Subtractor #(.width(2)) subtractor_2 (.a(register_2_q), .b(2'b01), .out(subtractor_2_out));  // open: bin, bout
endmodule

module HazardManager (
  input  [31:0] inst,
  input  [5:0] opcode2,
  input  clk,
  input  [4:0] rc2,
  input  [5:0] opcode3,
  input  [4:0] rc3,
  output HayHazard
);

  wire and_1_out, and_2_out, comparator_1_eq, hazardhandler_1_hazardout, hazardhandler_2_hazardout,
       hazardresolver_1_out_4, not_1_out;
  wire [4:0] rd, rs, rt;
  wire [5:0] opc;

  Comparator #(.width(32)) comparator_1 (.a({32{1'b0}}), .b(inst), .eq(comparator_1_eq));  // open: gt, lt
  Spliter spliter_1 (.ENTRADA(inst), .rt(rt), .opcode(opc), .rd(rd), .rs(rs));  // open: funct, sham, off, jump
  not not_1 (not_1_out, comparator_1_eq);
  HazardHandler hazardhandler_1 (
    .opcode1(opc), .opcode2(opcode2), .rt(rt), .rc(rc2), .rs(rs), .hazardout(hazardhandler_1_hazardout));
  HazardHandler hazardhandler_2 (
    .opcode1(opc), .opcode2(opcode3), .rt(rt), .rc(rc3), .rs(rs), .hazardout(hazardhandler_2_hazardout));
  and and_1 (and_1_out, not_1_out, hazardhandler_1_hazardout);
  and and_2 (and_2_out, not_1_out, hazardhandler_2_hazardout);
  HazardResolver hazardresolver_1 (
    .hazardin2(and_1_out), .clk(clk), .hazardin(and_2_out), .out_4(hazardresolver_1_out_4));
  not not_2 (HayHazard, hazardresolver_1_out_4);
endmodule

// Forwarding Unit
module ForwardUnit (
  input  [4:0] Rs,
  input  [4:0] rc_mesa3,
  input  regwrite_mesa3,
  input  [4:0] rc_mesa4,
  input  [4:0] Rt,
  input  Rgwrite_mesa_4,
  output [1:0] ForwardA,
  output [1:0] ForwardB
);

  wire comparator_1_eq, comparator_2_eq, comparator_3_eq, comparator_4_eq, comparator_5_eq, comparator_6_eq,
       comparator_7_eq, comparator_8_eq, not_1_out, not_2_out, not_3_out, not_4_out;
  wire [1:0] and_1_out, and_3_out;

  Comparator #(.width(5)) comparator_1 (.a(Rt), .b(rc_mesa3), .eq(comparator_1_eq));  // open: gt, lt
  Comparator #(.width(5)) comparator_2 (.a(rc_mesa3), .b({5{1'b0}}), .eq(comparator_2_eq));  // open: gt, lt
  Comparator #(.width(5)) comparator_3 (.a(Rt), .b(rc_mesa4), .eq(comparator_3_eq));  // open: gt, lt
  Comparator #(.width(5)) comparator_4 (.a(rc_mesa4), .b({5{1'b0}}), .eq(comparator_4_eq));  // open: gt, lt
  Comparator #(.width(5)) comparator_5 (.a(Rs), .b(rc_mesa3), .eq(comparator_5_eq));  // open: gt, lt
  Comparator #(.width(5)) comparator_6 (.a(rc_mesa3), .b({5{1'b0}}), .eq(comparator_6_eq));  // open: gt, lt
  Comparator #(.width(5)) comparator_7 (.a(Rs), .b(rc_mesa4), .eq(comparator_7_eq));  // open: gt, lt
  Comparator #(.width(5)) comparator_8 (.a(rc_mesa4), .b({5{1'b0}}), .eq(comparator_8_eq));  // open: gt, lt
  not not_1 (not_1_out, comparator_2_eq);
  not not_2 (not_2_out, comparator_4_eq);
  not not_3 (not_3_out, comparator_6_eq);
  not not_4 (not_4_out, comparator_8_eq);
  and and_1 (and_1_out[0], Rgwrite_mesa_4, comparator_3_eq, not_2_out);
  and and_2 (and_3_out[1], regwrite_mesa3, comparator_5_eq, not_3_out);
  and and_3 (and_3_out[0], Rgwrite_mesa_4, comparator_7_eq, not_4_out);
  and and_4 (and_1_out[1], regwrite_mesa3, comparator_1_eq, not_1_out);
  fw fw_1 (.xx(and_1_out), .fw(ForwardB));
  fw fw_2 (.xx(and_3_out), .fw(ForwardA));

  // Other names for the same wires on the sheet: rc3[4:0] = rc_mesa3; rc4[4:0] = rc_mesa4; rgw3 = regwrite_mesa3;
  //   rgw4 = Rgwrite_mesa_4
endmodule

module fw (
  input  [1:0] xx,
  output [1:0] fw
);

  wire not_1_out;

  not not_1 (not_1_out, xx[1]);
  and and_1 (fw[0], not_1_out, xx[0]);

  assign fw[1] = xx[1];
endmodule
